# Fritzing sketch Esquema Electrico HubUsbBotonesArduino (saved by Fritzing 0.9.3b)
breadboards: 1

parts:
  Componente1 = Arduino Nano (Rev3.0)
  S1 = Pushbutton [package="[THT]"]
  LED1 = LED - 5mm [color="Blue (525nm)" package="5 mm [THT]"]
  LED2 = LED - 5mm [color="Red (633nm)" package="5 mm [THT]"]
  4_Relay_Module1 = OPENMolo 4 Relay breakout board
  R3 = Resistor [tolerance=±5% resistance=220 package=THT]
  R1 = Resistor [tolerance=±5% resistance=220 package="2010 [SMD]"]
  R2 = Resistor [tolerance=±5% resistance=220 package="0805 [SMD]"]

nets:
  N1: Componente1.D2, S1.Pin_3, S1.Pin_4
  N2: Componente1.D4, 4_Relay_Module1.E4
  N3: Componente1.D5, 4_Relay_Module1.E3
  N4: Componente1.D6, 4_Relay_Module1.E2
  N5: Componente1.D7, 4_Relay_Module1.E1
  GND: Componente1.GND, LED1.cathode, LED2.cathode, 4_Relay_Module1.GND, R3.Pin_1
  5V: Componente1.5V, 4_Relay_Module1.VCC
  N6: Componente1.A2, R2.Pin_0
  N7: Componente1.A1, R1.Pin_0
  N8: Componente1.3V3, S1.Pin_1, S1.Pin_2, R3.Pin_0
  N9: LED1.anode, R1.Pin_1
  N10: LED2.anode, R2.Pin_1

custom parts:
  OPENMolo 4 Relay breakout board: Módulo de 8 relés de 10A optoaislados pensado para desarrollos rápidos basadon en microcontroladores o microcomputadoras. Estos módulos son diseñados con especial cuidado tanto en sus capacidades aisladoras para preservar equipos de mayor valor asi como en las fijaciones para evitar problemas a la hora de armar un prototipo o de fijarlo en un tablero definitivo. Una importante característica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
